// Logisim project 27 Bit minimal CPU.circ as structural Verilog: 27 circuits, main circuit main
module main (
);


  // Notes on the sheet:
  //   2207024
endmodule

// AND
module _27_Bit_AND (
  input  [26:0] A,
  input  [26:0] B,
  output [26:0] AB
);

  assign AB = A & B;  // AND_Gate and_1, 27 bits wide

  // Notes on the sheet:
  //   2207024
endmodule

// OR
module _27_Bit_OR (
  input  [26:0] A,
  input  [26:0] B,
  output [26:0] A_B
);

  assign A_B = A | B;  // OR_Gate or_1, 27 bits wide

  // Notes on the sheet:
  //   2207024
endmodule

// Zero
module Zero_Check (
  input  [26:0] A,
  output out_2
);

  wire or_1_out;

  or or_1 (or_1_out, A[0], A[1], A[2], A[3], A[4], A[5], A[6], A[7], A[8], A[9], A[10], A[11], A[12], A[13], A[14], A[15], A[16], A[17], A[18], A[19], A[20], A[21], A[22], A[23], A[24], A[25], A[26]);
  not not_1 (out_2, or_1_out);

  // Notes on the sheet:
  //   2207024
endmodule

module Negative_check (
  input  [26:0] A,
  output out_2
);


  assign out_2 = A[26];

  // Notes on the sheet:
  //   2207024
endmodule

module _3_bit_CLA_adder___subtractor (
  input  Cin,
  input  [2:0] A,
  input  [2:0] B,
  output s0,
  output s1,
  output s2,
  output c3,
  output c2
);

  wire and_4_out, and_5_out, and_6_out, and_7_out, and_8_out, and_9_out, C1, G0, G1, G2, P0, P1, P2;

  xor xor_1 (P0, B[0], A[0]);
  xor xor_2 (P1, B[1], A[1]);
  xor xor_3 (P2, B[2], A[2]);
  and and_1 (G0, B[0], A[0]);
  and and_2 (G1, B[1], A[1]);
  and and_3 (G2, B[2], A[2]);
  and and_4 (and_4_out, Cin, P0);
  and and_5 (and_5_out, G0, P1);
  and and_6 (and_6_out, P1, Cin, P0);
  and and_7 (and_7_out, G1, P2);
  and and_8 (and_8_out, P2, G0, P1);
  or or_1 (C1, and_4_out, G0);
  and and_9 (and_9_out, P0, P1, P2, Cin);
  or or_2 (c2, and_5_out, and_6_out, G1);
  or or_3 (c3, and_7_out, and_8_out, G2, and_9_out);
  _1_Bit_full_Adder u_1_bit_full_adder_1 (.A(A[0]), .B(B[0]), .C_in(Cin), .S(s0));
  _1_Bit_full_Adder u_1_bit_full_adder_2 (.A(A[1]), .B(B[1]), .C_in(C1), .S(s1));
  _1_Bit_full_Adder u_1_bit_full_adder_3 (.A(A[2]), .B(B[2]), .C_in(c2), .S(s2));

  // Notes on the sheet:
  //   2207024
endmodule

module _9_bit_cla_adder___sub (
  input  in_1,
  input  [8:0] A,
  input  [8:0] B,
  output [8:0] out_4,
  output out_5,
  output out_6
);

  wire n3_bit_cla_adder_subtractor_1_c3, n3_bit_cla_adder_subtractor_2_c3;

  _3_bit_CLA_adder___subtractor u_3_bit_cla_adder_subtractor_1 (
    .Cin(in_1), .A(A[2:0]), .B(B[2:0]), .s0(out_4[0]), .s1(out_4[1]), .s2(out_4[2]),
    .c3(n3_bit_cla_adder_subtractor_1_c3));  // open: c2
  _3_bit_CLA_adder___subtractor u_3_bit_cla_adder_subtractor_2 (
    .Cin(n3_bit_cla_adder_subtractor_1_c3), .A(A[5:3]), .B(B[5:3]), .s0(out_4[3]), .s1(out_4[4]),
    .s2(out_4[5]), .c3(n3_bit_cla_adder_subtractor_2_c3));  // open: c2
  _3_bit_CLA_adder___subtractor u_3_bit_cla_adder_subtractor_3 (
    .Cin(n3_bit_cla_adder_subtractor_2_c3), .A(A[8:6]), .B(B[8:6]), .c2(out_6), .s0(out_4[6]), .s1(out_4[7]),
    .s2(out_4[8]), .c3(out_5));

  // Notes on the sheet:
  //   2207024
endmodule

module _27_bit_CLA_adder__subtractor (
  input  in_1,
  input  [26:0] A,
  input  [26:0] B,
  output [26:0] out_4,
  output out_5,
  output out_6
);

  wire n9_bit_cla_adder_sub_1_out_5, n9_bit_cla_adder_sub_2_out_5, n9_bit_cla_adder_sub_3_out_6;
  wire [26:0] bit_extender_1_out, xor_1_out;

  assign xor_1_out = B ^ bit_extender_1_out;  // XOR_Gate xor_1, 27 bits wide
  assign bit_extender_1_out = {{26{in_1}}, in_1};  // Bit_Extender bit_extender_1
  _9_bit_cla_adder___sub u_9_bit_cla_adder_sub_1 (
    .in_1(in_1), .A(A[8:0]), .B(xor_1_out[8:0]), .out_4(out_4[8:0]), .out_5(n9_bit_cla_adder_sub_1_out_5));  // open: out_6
  _9_bit_cla_adder___sub u_9_bit_cla_adder_sub_2 (
    .in_1(n9_bit_cla_adder_sub_1_out_5), .A(A[17:9]), .B(xor_1_out[17:9]), .out_4(out_4[17:9]),
    .out_5(n9_bit_cla_adder_sub_2_out_5));  // open: out_6
  _9_bit_cla_adder___sub u_9_bit_cla_adder_sub_3 (
    .in_1(n9_bit_cla_adder_sub_2_out_5), .A(A[26:18]), .B(xor_1_out[26:18]),
    .out_6(n9_bit_cla_adder_sub_3_out_6), .out_4(out_4[26:18]), .out_5(out_5));
  xor xor_2 (out_6, n9_bit_cla_adder_sub_3_out_6, out_5);

  // Notes on the sheet:
  //   2207024
endmodule

module _27_BIT_ALU (
  input  [1:0] control,
  input  [26:0] A,
  input  [26:0] B,
  output [26:0] \output ,
  output zero,
  output neg,
  output carry,
  output overflow
);

  wire [26:0] n27_bit_and_1_ab, n27_bit_cla_adder_subtractor_1_out_4, n27_bit_or_1_a_b;

  _27_bit_CLA_adder__subtractor u_27_bit_cla_adder_subtractor_1 (
    .in_1(control[0]), .A(A), .B(B), .out_6(overflow), .out_4(n27_bit_cla_adder_subtractor_1_out_4),
    .out_5(carry));
  _27_Bit_AND u_27_bit_and_1 (.A(A), .B(B), .AB(n27_bit_and_1_ab));
  _27_Bit_OR u_27_bit_or_1 (.A(A), .B(B), .A_B(n27_bit_or_1_a_b));
  Multiplexer #(.select(2), .width(27), .enable("false")) multiplexer_1 (
    .in0(n27_bit_or_1_a_b), .in1(n27_bit_and_1_ab), .in2(n27_bit_cla_adder_subtractor_1_out_4),
    .in3(n27_bit_cla_adder_subtractor_1_out_4), .out(\output ), .sel(control));
  Zero_Check zero_check_1 (.A(\output ), .out_2(zero));
  Negative_check negative_check_1 (.A(\output ), .out_2(neg));

  // Notes on the sheet:
  //   A
  //   B
  //   2207024
  //   CONTROL
  //   CONTROL
  //   OUTPUT
  //   ZERO FLAG
  //   NEGATIVE FLAG
  //   CARRY FLAG
  //   Overflow Flag
  //   00
  //   01
  //   10
  //   11
  //   FUNCTION
  //   - OR
  //   - AND
  //   - ADDER
  //   - SUBTRACTOR
endmodule

module _1_Bit_full_Adder (
  input  A,
  input  B,
  input  C_in,
  output S
);

  wire xor_1_out;

  xor xor_1 (xor_1_out, A, B);
  xor xor_2 (S, xor_1_out, C_in);
endmodule

module IR (
  input  LOAD,
  input  [3:0] in_2,
  input  clk,
  input  clr,
  output [3:0] out_5
);

  wire and_1_out, and_2_out, and_3_out, and_4_out, and_5_out, and_6_out, and_7_out, and_8_out, not_1_out,
       not_2_out, not_3_out, not_4_out;

  not not_1 (not_1_out, in_2[0]);
  not not_2 (not_2_out, in_2[1]);
  not not_3 (not_3_out, in_2[2]);
  not not_4 (not_4_out, in_2[3]);
  and and_1 (and_1_out, in_2[0], LOAD);
  and and_2 (and_2_out, not_1_out, LOAD);
  and and_3 (and_3_out, in_2[1], LOAD);
  and and_4 (and_4_out, not_2_out, LOAD);
  and and_5 (and_5_out, in_2[2], LOAD);
  and and_6 (and_6_out, not_3_out, LOAD);
  and and_7 (and_7_out, in_2[3], LOAD);
  and and_8 (and_8_out, not_4_out, LOAD);
  J_K_Flip_Flop j_k_ff_1 (.J(and_1_out), .clk(clk), .K(and_2_out), .Q(out_5[0]), .reset(clr));  // open: Qn, preset, en
  J_K_Flip_Flop j_k_ff_2 (.J(and_3_out), .clk(clk), .K(and_4_out), .Q(out_5[1]), .reset(clr));  // open: Qn, preset, en
  J_K_Flip_Flop j_k_ff_3 (.J(and_5_out), .clk(clk), .K(and_6_out), .Q(out_5[2]), .reset(clr));  // open: Qn, preset, en
  J_K_Flip_Flop j_k_ff_4 (.J(and_7_out), .clk(clk), .K(and_8_out), .Q(out_5[3]), .reset(clr));  // open: Qn, preset, en

  // Other names for the same wires on the sheet: _0 = in_2[0]; _1 = in_2[1]; _2 = in_2[2]; _3 = in_2[3]

  // Notes on the sheet:
  //   2207024
endmodule

module _6_bit_load_counter (
  input  count,
  input  load,
  input  [5:0] in_3,
  input  clk,
  input  clr,
  output [5:0] out_6,
  output cout
);

  wire and_1_out, and_2_out, and_3_out, and_4_out, and_5_out, and_6_out, and_7_out, and_8_out, and_9_out,
       and_10_out, and_11_out, and_12_out, and_13_out, and_14_out, and_15_out, and_16_out, and_17_out,
       and_18_out, not_1_out, not_2_out, not_3_out, not_4_out, not_5_out, not_6_out, not_7_out, or_1_out,
       or_2_out, or_3_out, or_4_out, or_5_out, or_6_out, or_7_out, or_8_out, or_9_out, or_10_out, or_11_out,
       or_12_out;

  not not_1 (not_1_out, load);
  and and_1 (and_1_out, count, not_1_out);
  not not_2 (not_2_out, in_3[0]);
  not not_3 (not_3_out, in_3[1]);
  not not_4 (not_4_out, in_3[2]);
  not not_5 (not_5_out, in_3[3]);
  not not_6 (not_6_out, in_3[4]);
  not not_7 (not_7_out, in_3[5]);
  and and_2 (and_2_out, load, in_3[0]);
  and and_3 (and_3_out, load, not_2_out);
  and and_4 (and_4_out, load, in_3[1]);
  and and_5 (and_5_out, load, not_3_out);
  and and_6 (and_6_out, load, in_3[2]);
  and and_7 (and_7_out, load, not_4_out);
  and and_8 (and_8_out, load, in_3[3]);
  and and_9 (and_9_out, load, not_5_out);
  and and_10 (and_10_out, load, in_3[4]);
  and and_11 (and_11_out, load, not_6_out);
  and and_12 (and_12_out, load, in_3[5]);
  and and_13 (and_13_out, load, not_7_out);
  and and_14 (and_14_out, and_1_out, out_6[0]);
  and and_15 (and_15_out, and_1_out, out_6[0], out_6[1]);
  and and_16 (and_16_out, and_1_out, out_6[0], out_6[1], out_6[2]);
  and and_17 (and_17_out, and_1_out, out_6[0], out_6[1], out_6[2], out_6[3]);
  and and_18 (and_18_out, and_1_out, out_6[0], out_6[1], out_6[2], out_6[3], out_6[4]);
  and and_19 (cout, and_1_out, out_6[0], out_6[1], out_6[2], out_6[3], out_6[4], out_6[5]);
  or or_1 (or_1_out, and_2_out, and_1_out);
  or or_2 (or_2_out, and_1_out, and_3_out);
  or or_3 (or_3_out, and_4_out, and_14_out);
  or or_4 (or_4_out, and_14_out, and_5_out);
  or or_5 (or_5_out, and_6_out, and_15_out);
  or or_6 (or_6_out, and_15_out, and_7_out);
  or or_7 (or_7_out, and_8_out, and_16_out);
  or or_8 (or_8_out, and_16_out, and_9_out);
  or or_9 (or_9_out, and_10_out, and_17_out);
  or or_10 (or_10_out, and_17_out, and_11_out);
  or or_11 (or_11_out, and_12_out, and_18_out);
  or or_12 (or_12_out, and_18_out, and_13_out);
  J_K_Flip_Flop j_k_ff_1 (.J(or_1_out), .clk(clk), .K(or_2_out), .Q(out_6[0]), .reset(clr));  // open: Qn, preset, en
  J_K_Flip_Flop j_k_ff_2 (.J(or_3_out), .clk(clk), .K(or_4_out), .Q(out_6[1]), .reset(clr));  // open: Qn, preset, en
  J_K_Flip_Flop j_k_ff_3 (.J(or_5_out), .clk(clk), .K(or_6_out), .Q(out_6[2]), .reset(clr));  // open: Qn, preset, en
  J_K_Flip_Flop j_k_ff_4 (.J(or_7_out), .clk(clk), .K(or_8_out), .Q(out_6[3]), .reset(clr));  // open: Qn, preset, en
  J_K_Flip_Flop j_k_ff_5 (.J(or_9_out), .clk(clk), .K(or_10_out), .Q(out_6[4]), .reset(clr));  // open: Qn, preset, en
  J_K_Flip_Flop j_k_ff_6 (.J(or_11_out), .clk(clk), .K(or_12_out), .Q(out_6[5]), .reset(clr));  // open: Qn, preset, en

  // Notes on the sheet:
  //   2207024
endmodule

module _6_bit_load_reg (
  input  load,
  input  [5:0] in_2,
  input  clk,
  input  clr,
  output [5:0] out_5
);

  wire and_1_out, and_2_out, and_3_out, and_4_out, and_5_out, and_6_out, and_7_out, and_8_out, and_9_out,
       and_10_out, and_11_out, and_12_out, load_not, load_t, or_1_out, or_2_out, or_3_out, or_4_out,
       or_5_out, or_6_out;

  not not_1 (load_not, load);
  not not_2 (load_t, load_not);
  and and_1 (and_1_out, out_5[0], load_not);
  and and_2 (and_2_out, in_2[0], load_t);
  and and_3 (and_3_out, out_5[1], load_not);
  and and_4 (and_4_out, in_2[1], load_t);
  and and_5 (and_5_out, out_5[2], load_not);
  and and_6 (and_6_out, in_2[2], load_t);
  and and_7 (and_7_out, out_5[3], load_not);
  and and_8 (and_8_out, in_2[3], load_t);
  and and_9 (and_9_out, out_5[4], load_not);
  and and_10 (and_10_out, in_2[4], load_t);
  and and_11 (and_11_out, out_5[5], load_not);
  and and_12 (and_12_out, in_2[5], load_t);
  or or_1 (or_1_out, and_1_out, and_2_out);
  or or_2 (or_2_out, and_3_out, and_4_out);
  or or_3 (or_3_out, and_5_out, and_6_out);
  or or_4 (or_4_out, and_7_out, and_8_out);
  or or_5 (or_5_out, and_9_out, and_10_out);
  or or_6 (or_6_out, and_11_out, and_12_out);
  D_Flip_Flop d_ff_1 (.clk(clk), .D(or_1_out), .Q(out_5[0]), .reset(clr));  // open: Qn, preset, en
  D_Flip_Flop d_ff_2 (.clk(clk), .D(or_2_out), .Q(out_5[1]), .reset(clr));  // open: Qn, preset, en
  D_Flip_Flop d_ff_3 (.clk(clk), .D(or_3_out), .Q(out_5[2]), .reset(clr));  // open: Qn, preset, en
  D_Flip_Flop d_ff_4 (.clk(clk), .D(or_4_out), .Q(out_5[3]), .reset(clr));  // open: Qn, preset, en
  D_Flip_Flop d_ff_5 (.clk(clk), .D(or_5_out), .Q(out_5[4]), .reset(clr));  // open: Qn, preset, en
  D_Flip_Flop d_ff_6 (.clk(clk), .D(or_6_out), .Q(out_5[5]), .reset(clr));  // open: Qn, preset, en

  // Notes on the sheet:
  //   Load
  //   2207024
endmodule

module AC (
  input  load,
  input  [26:0] in_2,
  input  clk,
  input  clr,
  output [26:0] out_5
);

  _6_bit_load_reg u_6_bit_load_reg_1 (.load(load), .in_2(in_2[5:0]), .clk(clk), .clr(clr), .out_5(out_5[5:0]));
  _6_bit_load_reg u_6_bit_load_reg_2 (.load(load), .in_2(in_2[11:6]), .clk(clk), .clr(clr), .out_5(out_5[11:6]));
  _6_bit_load_reg u_6_bit_load_reg_3 (.load(load), .in_2(in_2[17:12]), .clk(clk), .clr(clr), .out_5(out_5[17:12]));
  _6_bit_load_reg u_6_bit_load_reg_4 (.load(load), .in_2(in_2[23:18]), .clk(clk), .clr(clr), .out_5(out_5[23:18]));
  _1_bit__load_resistor u_1_bit_load_resistor_1 (.LOAD(load), .in_2(in_2[24]), .CLK(clk), .CLR(clr), .out_5(out_5[24]));
  _1_bit__load_resistor u_1_bit_load_resistor_2 (.LOAD(load), .in_2(in_2[25]), .CLK(clk), .CLR(clr), .out_5(out_5[25]));
  _1_bit__load_resistor u_1_bit_load_resistor_3 (.LOAD(load), .in_2(in_2[26]), .CLK(clk), .CLR(clr), .out_5(out_5[26]));

  // Notes on the sheet:
  //   2207024
endmodule

module _1_bit__load_resistor (
  input  LOAD,
  input  in_2,
  input  CLK,
  input  CLR,
  output out_5
);

  wire and_1_out, and_2_out, not_1_out, or_1_out;

  and and_1 (and_1_out, out_5, not_1_out);
  not not_1 (not_1_out, LOAD);
  and and_2 (and_2_out, LOAD, in_2);
  or or_1 (or_1_out, and_1_out, and_2_out);
  D_Flip_Flop d_ff_1 (.clk(CLK), .D(or_1_out), .Q(out_5), .reset(CLR));  // open: Qn, preset, en

  // Notes on the sheet:
  //   2207024
endmodule

module MBR (
  input  count,
  input  load,
  input  [26:0] in_3,
  input  clk,
  input  clr,
  output [26:0] out_6
);

  wire n6_bit_load_counter_1_cout, n6_bit_load_counter_2_cout, n6_bit_load_counter_3_cout,
       n6_bit_load_counter_4_cout;

  _6_bit_load_counter u_6_bit_load_counter_1 (
    .count(count), .load(load), .in_3(in_3[5:0]), .clk(clk), .clr(clr), .out_6(out_6[5:0]),
    .cout(n6_bit_load_counter_1_cout));
  _6_bit_load_counter u_6_bit_load_counter_2 (
    .count(n6_bit_load_counter_1_cout), .load(load), .in_3(in_3[11:6]), .clk(clk), .clr(clr),
    .out_6(out_6[11:6]), .cout(n6_bit_load_counter_2_cout));
  _6_bit_load_counter u_6_bit_load_counter_3 (
    .count(n6_bit_load_counter_2_cout), .load(load), .in_3(in_3[17:12]), .clk(clk), .clr(clr),
    .out_6(out_6[17:12]), .cout(n6_bit_load_counter_3_cout));
  _6_bit_load_counter u_6_bit_load_counter_4 (
    .count(n6_bit_load_counter_3_cout), .load(load), .in_3(in_3[23:18]), .clk(clk), .clr(clr),
    .out_6(out_6[23:18]), .cout(n6_bit_load_counter_4_cout));
  _3__bit_load_counter u_3_bit_load_counter_1 (
    .Cin(n6_bit_load_counter_4_cout), .count(count), .LOAD(load), .in_4(in_3[26:24]), .CLK(clk), .CLR(clr),
    .out_7(out_6[26:24]));

  // Notes on the sheet:
  //   2207024
endmodule

module _3__bit_load_counter (
  input  Cin,
  input  count,
  input  LOAD,
  input  [2:0] in_4,
  input  CLK,
  input  CLR,
  output [2:0] out_7
);

  wire and_1_out, and_2_out, and_3_out, and_4_out, and_5_out, and_6_out, and_7_out, and_8_out, and_9_out,
       and_10_out, not_1_out, not_2_out, not_3_out, not_4_out, or_1_out, or_2_out, or_3_out, or_4_out,
       or_5_out, or_6_out;

  not not_1 (not_1_out, LOAD);
  and and_1 (and_1_out, count, not_1_out);
  not not_2 (not_2_out, in_4[0]);
  not not_3 (not_3_out, in_4[1]);
  not not_4 (not_4_out, in_4[2]);
  and and_2 (and_2_out, LOAD, in_4[0]);
  and and_3 (and_3_out, LOAD, not_2_out);
  and and_4 (and_4_out, LOAD, in_4[1]);
  and and_5 (and_5_out, LOAD, not_3_out);
  and and_6 (and_6_out, LOAD, in_4[2]);
  and and_7 (and_7_out, LOAD, not_4_out);
  and and_8 (and_8_out, and_1_out, Cin);
  and and_9 (and_9_out, and_1_out, Cin, out_7[0]);
  and and_10 (and_10_out, out_7[0], and_1_out, Cin, out_7[1]);
  or or_1 (or_1_out, and_2_out, and_8_out);
  or or_2 (or_2_out, and_8_out, and_3_out);
  or or_3 (or_3_out, and_4_out, and_9_out);
  or or_4 (or_4_out, and_9_out, and_5_out);
  or or_5 (or_5_out, and_6_out, and_10_out);
  or or_6 (or_6_out, and_10_out, and_7_out);
  J_K_Flip_Flop j_k_ff_1 (.J(or_1_out), .clk(CLK), .K(or_2_out), .Q(out_7[0]), .reset(CLR));  // open: Qn, preset, en
  J_K_Flip_Flop j_k_ff_2 (.J(or_3_out), .clk(CLK), .K(or_4_out), .Q(out_7[1]), .reset(CLR));  // open: Qn, preset, en
  J_K_Flip_Flop j_k_ff_3 (.J(or_5_out), .clk(CLK), .K(or_6_out), .Q(out_7[2]), .reset(CLR));  // open: Qn, preset, en

  // Notes on the sheet:
  //   2207024 
endmodule

module ALL_REG (
  input  [26:0] in_1,
  input  [3:0] in_2,
  input  Count,
  input  Load,
  input  [5:0] in_5,
  input  in_6,
  output [26:0] out_7,
  output [3:0] out_8,
  output [5:0] out_9,
  output [26:0] out_10,
  output [5:0] out_11
);

  wire clock_1_out;

  Clock clock_1 (.out(clock_1_out));
  MBR mbr_1 (.count(Count), .load(Load), .in_3(in_1), .clk(clock_1_out), .clr(in_6), .out_6(out_7));
  IR ir_1 (.LOAD(Load), .in_2(in_2), .clk(clock_1_out), .clr(in_6), .out_5(out_8));
  MAR mar_1 (.load(Load), .in_2(in_5), .clk(clock_1_out), .clr(in_6), .out_5(out_9));
  AC ac_1 (.load(Load), .in_2(in_1), .clk(clock_1_out), .clr(in_6), .out_5(out_10));
  PC pc_1 (.count(Count), .load(Load), .in_3(in_5), .clk(clock_1_out), .clr(in_6), .out_6(out_11));  // open: cout
  // Probe on out_7
  // Probe on out_8
  // Probe on out_9
  // Probe on out_10
  // Probe on out_11

  // Notes on the sheet:
  //   2207024
  //   MBR
  //   AC
  //   PC
  //   IR
  //   MAR
  //   MBR
  //   IR
  //   MAR
  //   AC
  //   PC
endmodule

module Control_Unit (
  input  [26:0] Data_in,
  input  resset,
  input  clk,
  output [26:0] Data_out,
  output OUT_clk,
  output load,
  output [5:0] out_7,
  output [26:0] BUFFER,
  output [26:0] ACCUMULATOR,
  output Store
);

  wire _2_s_compliment, _2CMP, Acc_to_MBR, ADD, ADD_ALU, AND, and_9_out, AND_ALU, BSB, BUN, Change_OP_0101,
       F, F1, F2, F_prime, HLT, INC2, INC_ALU, ISZ, LOAD_t, MBR_inc, MBR_to_Acc, MBR_to_IR, MBR_to_MAR,
       MBR_to_Mem_1, MBR_to_Mem_2, MBR_to_Mem_3, MBR_to_PC_1, MBR_Zerooo, Mem_to_MBR_1, Mem_to_MBR_2,
       not_2_out, or_2_out, or_3_out, or_5_out, or_6_out, or_7_out, or_8_out, or_9_out, or_10_out, or_11_out,
       or_12_out, PC_inc_2, PC_to_MAR, RT_SHFT, SHR, STO, t0, t1, t2, t3;
  wire [1:0] counter_1_q, selection_line_for_alu_1_out_3;
  wire [3:0] bit_extender_1_out, IR_out;
  wire [5:0] multiplexer_5_out, multiplexer_8_out;
  wire [23:0] New_MBR;
  wire [26:0] ACC_in, ACC_in_2_s_cmp, ACC_in_RTSH, double_increment_1_out_2, multiplexer_1_out,
       multiplexer_4_out, multiplexer_6_out, multiplexer_7_out, multiplexer_9_out, n2_s_compliment_1_out_2,
       n27_bit_alu_1_output;

  and and_1 (PC_to_MAR, F_prime, t0);
  or or_1 (load, Mem_to_MBR_1, Mem_to_MBR_2);
  Counter #(.width(2), .max('h3)) counter_1 (
    .Q(counter_1_q), .clk(OUT_clk), .clr(resset));  // open: load, D, count, carry
  and and_2 (MBR_to_MAR, F, t0);
  and and_3 (AND_ALU, F, AND, t2);
  and and_4 (INC_ALU, F, INC2, t2);
  and and_5 (_2_s_compliment, F, _2CMP, t2);
  or or_2 (or_2_out, load, Change_OP_0101, Acc_to_MBR);
  Multiplexer #(.select(2), .width(27), .enable("false")) multiplexer_1 (
    .in0(Data_in), .in1({3'b000, New_MBR[23:20], {14{1'b0}}, New_MBR[5:0]}), .in2(ACCUMULATOR),
    .out(multiplexer_1_out), .sel({Acc_to_MBR, Change_OP_0101}));  // open: in3
  or or_3 (or_3_out, ADD_ALU, AND_ALU);
  or or_4 (Store, MBR_to_Mem_3, MBR_to_Mem_1, MBR_to_Mem_2);
  Decoder #(.select(2), .enable("false")) decoder_1 (.out0(t0), .out1(t1), .out2(t2), .out3(t3), .sel(counter_1_q));
  and and_6 (MBR_inc, F, ISZ, t2);
  and and_7 (Change_OP_0101, F, BSB, t2);
  and and_8 (MBR_to_Acc, F, LOAD_t, t2);
  or or_5 (or_5_out, BUFFER[0], BUFFER[1], BUFFER[2], BUFFER[3], BUFFER[4], BUFFER[5], BUFFER[6], BUFFER[7], BUFFER[8], BUFFER[9], BUFFER[10], BUFFER[11], BUFFER[12], BUFFER[13], BUFFER[14], BUFFER[15], BUFFER[16], BUFFER[17], BUFFER[18], BUFFER[19], BUFFER[20], BUFFER[21], BUFFER[22], BUFFER[23], BUFFER[24], BUFFER[25], BUFFER[26]);
  not not_1 (MBR_Zerooo, or_5_out);
  and and_9 (and_9_out, or_3_out, t2);
  Selection_line_for_ALU selection_line_for_alu_1 (
    .\and (AND_ALU), .add(ADD_ALU), .out_3(selection_line_for_alu_1_out_3));
  Multiplexer #(.width(27), .enable("false")) multiplexer_2 (.in0(Data_in), .in1(BUFFER), .out(Data_out), .sel(Store));
  and and_10 (OUT_clk, clk, not_2_out);
  not not_2 (not_2_out, HLT);
  and and_11 (Mem_to_MBR_1, F_prime, t1);
  MBR MBR (.count(MBR_inc), .load(or_2_out), .in_3(multiplexer_1_out), .clk(OUT_clk), .clr(resset), .out_6(BUFFER));
  _27_BIT_ALU u_27_bit_alu_1 (
    .control(selection_line_for_alu_1_out_3), .A(ACCUMULATOR), .B(BUFFER), .\output (n27_bit_alu_1_output));  // open: zero, neg, carry, overflow
  or or_6 (or_6_out, BSB, AND, ADD, STO, ISZ, LOAD_t, HLT, INC2, SHR, _2CMP);
  // Probe on BUFFER
  Multiplexer #(.width(27), .enable("false")) multiplexer_3 (
    .in0(ACCUMULATOR), .in1(n27_bit_alu_1_output), .out(ACC_in), .sel(and_9_out));
  J_K_Flip_Flop j_k_ff_1 (.J(F1), .clk(OUT_clk), .K(F2), .Q(F));  // open: Qn, preset, en, reset
  not not_3 (F_prime, F);
  and and_12 (F2, F, t3);
  and and_13 (MBR_to_Mem_2, F, ISZ, t3);
  and and_14 (F1, F_prime, or_6_out, t3);
  and and_15 (ADD_ALU, F, ADD, t2);
  Multiplexer #(.width(27), .enable("false")) multiplexer_4 (
    .in0(ACC_in), .in1(ACC_in_2_s_cmp), .out(multiplexer_4_out), .sel(_2_s_compliment));
  and and_16 (MBR_to_IR, F_prime, t2);
  Multiplexer #(.width(6), .enable("false")) multiplexer_5 (
    .in0(New_MBR[5:0]), .in1(BUFFER[5:0]), .out(multiplexer_5_out), .sel(MBR_to_MAR));
  or or_7 (or_7_out, MBR_to_PC_1, Change_OP_0101);
  Multiplexer #(.width(27), .enable("false")) multiplexer_6 (
    .in0(multiplexer_4_out), .in1(ACC_in_RTSH), .out(multiplexer_6_out), .sel(RT_SHFT));
  and and_17 (MBR_to_Mem_1, F, BSB, t3);
  Multiplexer #(.width(27), .enable("false")) multiplexer_7 (
    .in0(multiplexer_6_out), .in1(double_increment_1_out_2), .out(multiplexer_7_out), .sel(INC_ALU));
  Double_Increment double_increment_1 (.Double_INC(ACCUMULATOR), .out_2(double_increment_1_out_2));
  and and_18 (PC_inc_2, F, ISZ, t3, MBR_Zerooo);
  and and_19 (RT_SHFT, F, SHR, t2);
  or or_8 (or_8_out, PC_to_MAR, MBR_to_MAR);
  MAR MAR (.load(or_8_out), .in_2(multiplexer_5_out), .clk(OUT_clk), .clr(resset), .out_5(out_7));
  Decoder #(.select(4), .enable("false")) decoder_2 (
    .out0(AND), .out1(ADD), .out2(STO), .out3(ISZ), .out4(BSB), .out5(BUN), .out6(LOAD_t), .out7(HLT),
    .out8(INC2), .out9(SHR), .out10(_2CMP), .sel(IR_out));  // open: out11, out12, out13, out14, out15
  or or_9 (or_9_out, Mem_to_MBR_1, PC_inc_2, MBR_to_Mem_1);
  Multiplexer #(.width(6), .enable("false")) multiplexer_8 (
    .in0(out_7), .in1(BUFFER[5:0]), .out(multiplexer_8_out), .sel(MBR_to_PC_1));
  Multiplexer #(.width(27), .enable("false")) multiplexer_9 (
    .in0(multiplexer_7_out), .in1(BUFFER), .out(multiplexer_9_out), .sel(MBR_to_Acc));
  assign bit_extender_1_out = {{3{Change_OP_0101}}, Change_OP_0101};  // Bit_Extender bit_extender_1
  assign New_MBR[23:20] = bit_extender_1_out & 4'b0101;  // AND_Gate and_20, 4 bits wide
  Right_shift right_shift_1 (
    .in_1(ACCUMULATOR), .t1(t1), .RHS(RT_SHFT), .clk(OUT_clk), .reset(resset), .out_6(ACC_in_RTSH));
  and and_21 (MBR_to_PC_1, BUN, t3);
  or or_10 (or_10_out, AND, ADD, ISZ, _2CMP, LOAD_t, INC2, SHR);
  PC PC (
    .count(or_9_out), .load(or_7_out), .in_3(multiplexer_8_out), .clk(OUT_clk), .clr(resset),
    .out_6(New_MBR[5:0]));  // open: cout
  or or_11 (or_11_out, INC_ALU, AND_ALU, MBR_to_Acc, ADD_ALU);
  and and_22 (Mem_to_MBR_2, F, or_10_out, t1);
  and and_23 (Acc_to_MBR, F, STO, t2);
  and and_24 (MBR_to_Mem_3, F, STO, t3);
  or or_12 (or_12_out, _2_s_compliment, RT_SHFT, or_11_out);
  AC Acc (.load(or_12_out), .in_2(multiplexer_9_out), .clk(OUT_clk), .clr(resset), .out_5(ACCUMULATOR));
  Multiplexer #(.width(27), .enable("false")) multiplexer_10 ();  // open: in0, in1, out, sel
  IR IR (.LOAD(MBR_to_IR), .in_2(BUFFER[23:20]), .clk(OUT_clk), .clr(resset), .out_5(IR_out));
  // Probe on ACCUMULATOR
  _2_s_comp_load_reg u_2_s_comp_load_reg_1 (
    .load(t1), .in_2(n2_s_compliment_1_out_2), .clk(OUT_clk), .clr(resset), .out_5(ACC_in_2_s_cmp));
  _2_s_compliment u_2_s_compliment_1 (.in_1(ACCUMULATOR), .out_2(n2_s_compliment_1_out_2));

  // Other names for the same wires on the sheet: MAR_to_PC = Change_OP_0101; PC_to_MBR = Change_OP_0101;
  //   ACC_out[26:0] = ACCUMULATOR; Clk_t = OUT_clk; MAR_out[5:0] = out_7; addr[5:0] = BUFFER[5:0];
  //   MBR_out[26:0] = BUFFER; opcode[3:0] = BUFFER[23:20]; PC_out[5:0] = New_MBR[5:0]; PC_inc_1 = Mem_to_MBR_1;
  //   PC_inc_3 = MBR_to_Mem_1; Reset = resset

  // Notes on the sheet:
  //   2207024
  //   Clock Circuit
  //   Equations
  //   AND CIRCUIT
  //   ISZ CIRCUIT
  //   BSB CIRCUIT
  //   LOAD CIRCUIT
  //   INC  CIRCUIT
  //   MBR
  //   2's Compliment CIRCUIT
  //   ALU
  //   IN and OUT pins
  //   ADD CIRCUIT
  //   Registers
  //   Fetch Cycle
  //   Execution Cycle
  //   MAR
  //   PC
  //   Right Shift  CIRCUIT
  //   Acc
  //   STO CIRCUIT
  //   IR
endmodule

module PC (
  input  count,
  input  load,
  input  [5:0] in_3,
  input  clk,
  input  clr,
  output [5:0] out_6,
  output cout
);

  _6_bit_load_counter u_6_bit_load_counter_1 (
    .count(count), .load(load), .in_3(in_3), .clk(clk), .clr(clr), .out_6(out_6), .cout(cout));
endmodule

module MAR (
  input  load,
  input  [5:0] in_2,
  input  clk,
  input  clr,
  output [5:0] out_5
);

  _6_bit_load_reg u_6_bit_load_reg_1 (.load(load), .in_2(in_2), .clk(clk), .clr(clr), .out_5(out_5));
endmodule

module Selection_line_for_ALU (
  input  \and ,
  input  add,
  output [1:0] out_3
);


  assign out_3 = {add, \and };
endmodule

module CPU (
  input  in_1,
  output [26:0] MBR,
  output [26:0] Acc
);

  wire clk_out, control_unit_1_load, control_unit_1_out_clk, control_unit_1_store;
  wire [5:0] control_unit_1_out_7;
  wire [26:0] control_unit_1_data_out, ram_1_data;

  Clock clk (.out(clk_out));
  // Probe on MBR
  Control_Unit control_unit_1 (
    .Data_in(ram_1_data), .resset(in_1), .clk(clk_out), .BUFFER(MBR), .ACCUMULATOR(Acc),
    .Data_out(control_unit_1_data_out), .OUT_clk(control_unit_1_out_clk), .load(control_unit_1_load),
    .out_7(control_unit_1_out_7), .Store(control_unit_1_store));
  // Probe on Acc
  RAM #(.addrWidth(6), .dataWidth(27), .bus("separate")) ram_1 (
    .addr(control_unit_1_out_7), .din(control_unit_1_data_out), .data(ram_1_data),
    .str(control_unit_1_store), .clk(control_unit_1_out_clk), .ld(control_unit_1_load));  // open: sel, clr

  // Notes on the sheet:
  //   2207024
endmodule

module Double_Increment (
  input  [26:0] Double_INC,
  output [26:0] out_2
);

  _27_BIT_ALU u_27_bit_alu_1 (
    .control(2'b10), .A(Double_INC), .B(27'h2), .\output (out_2));  // open: zero, neg, carry, overflow

  // Notes on the sheet:
  //   2207024
endmodule

module Right_shift (
  input  [26:0] in_1,
  input  t1,
  input  RHS,
  input  clk,
  input  reset,
  output [26:0] out_6
);

  wire not_1_out;

  not not_1 (not_1_out, clk);
  Shift_Register #(.length(27)) shift_register_1 (
    .shift(RHS), .in(1'b0), .clk(not_1_out), .load(t1), .clr(reset), .d0(in_1[26]), .q0(out_6[26]),
    .d1(in_1[25]), .q1(out_6[25]), .d2(in_1[24]), .q2(out_6[24]), .d3(in_1[23]), .q3(out_6[23]),
    .d4(in_1[22]), .q4(out_6[22]), .d5(in_1[21]), .q5(out_6[21]), .d6(in_1[20]), .q6(out_6[20]),
    .d7(in_1[19]), .q7(out_6[19]), .d8(in_1[18]), .q8(out_6[18]), .d9(in_1[17]), .q9(out_6[17]),
    .d10(in_1[16]), .q10(out_6[16]), .d11(in_1[15]), .q11(out_6[15]), .d12(in_1[14]), .q12(out_6[14]),
    .d13(in_1[13]), .q13(out_6[13]), .d14(in_1[12]), .q14(out_6[12]), .d15(in_1[11]), .q15(out_6[11]),
    .d16(in_1[10]), .q16(out_6[10]), .d17(in_1[9]), .q17(out_6[9]), .d18(in_1[8]), .q18(out_6[8]),
    .d19(in_1[7]), .q19(out_6[7]), .d20(in_1[6]), .q20(out_6[6]), .d21(in_1[5]), .q21(out_6[5]),
    .d22(in_1[4]), .q22(out_6[4]), .d23(in_1[3]), .q23(out_6[3]), .d24(in_1[2]), .q24(out_6[2]),
    .d25(in_1[1]), .q25(out_6[1]), .d26(in_1[0]), .q26(out_6[0]));  // open: out

  // Notes on the sheet:
  //   2207024
endmodule

module _2_s_compliment (
  input  [26:0] in_1,
  output [26:0] out_2
);

  wire [26:0] not_1_out;

  not not_1 (not_1_out[0], in_1[0]);
  not not_2 (not_1_out[1], in_1[1]);
  not not_3 (not_1_out[2], in_1[2]);
  not not_4 (not_1_out[3], in_1[3]);
  not not_5 (not_1_out[4], in_1[4]);
  not not_6 (not_1_out[5], in_1[5]);
  not not_7 (not_1_out[6], in_1[6]);
  not not_8 (not_1_out[7], in_1[7]);
  not not_9 (not_1_out[8], in_1[8]);
  not not_10 (not_1_out[9], in_1[9]);
  not not_11 (not_1_out[10], in_1[10]);
  not not_12 (not_1_out[11], in_1[11]);
  not not_13 (not_1_out[12], in_1[12]);
  not not_14 (not_1_out[13], in_1[13]);
  not not_15 (not_1_out[14], in_1[14]);
  not not_16 (not_1_out[15], in_1[15]);
  not not_17 (not_1_out[16], in_1[16]);
  not not_18 (not_1_out[17], in_1[17]);
  not not_19 (not_1_out[18], in_1[18]);
  not not_20 (not_1_out[19], in_1[19]);
  not not_21 (not_1_out[20], in_1[20]);
  not not_22 (not_1_out[21], in_1[21]);
  not not_23 (not_1_out[22], in_1[22]);
  not not_24 (not_1_out[23], in_1[23]);
  not not_25 (not_1_out[24], in_1[24]);
  not not_26 (not_1_out[25], in_1[25]);
  not not_27 (not_1_out[26], in_1[26]);
  _27_BIT_ALU u_27_bit_alu_1 (
    .control(2'b10), .A(not_1_out), .B(27'h1), .\output (out_2));  // open: zero, neg, carry, overflow

  // Notes on the sheet:
  //   2207024
endmodule

module _2_s_comp_load_reg (
  input  load,
  input  [26:0] in_2,
  input  clk,
  input  clr,
  output [26:0] out_5
);

  _6_bit_load_reg u_6_bit_load_reg_1 (.load(load), .in_2(in_2[5:0]), .clk(clk), .clr(clr), .out_5(out_5[5:0]));
  _6_bit_load_reg u_6_bit_load_reg_2 (.load(load), .in_2(in_2[11:6]), .clk(clk), .clr(clr), .out_5(out_5[11:6]));
  _6_bit_load_reg u_6_bit_load_reg_3 (.load(load), .in_2(in_2[17:12]), .clk(clk), .clr(clr), .out_5(out_5[17:12]));
  _6_bit_load_reg u_6_bit_load_reg_4 (.load(load), .in_2(in_2[23:18]), .clk(clk), .clr(clr), .out_5(out_5[23:18]));
  _1_bit__load_resistor u_1_bit_load_resistor_1 (.LOAD(load), .in_2(in_2[24]), .CLK(clk), .CLR(clr), .out_5(out_5[24]));
  _1_bit__load_resistor u_1_bit_load_resistor_2 (.LOAD(load), .in_2(in_2[25]), .CLK(clk), .CLR(clr), .out_5(out_5[25]));
  _1_bit__load_resistor u_1_bit_load_resistor_3 (.LOAD(load), .in_2(in_2[26]), .CLK(clk), .CLR(clr), .out_5(out_5[26]));

  // Notes on the sheet:
  //   2207024
endmodule
